# Fritzing sketch SD_DATE (saved by Fritzing 0.9.3b)
breadboards: 1

parts:
  S1 = Pushbutton [package="[THT]"]
  PCB2 = RTC_DS1302_module
  R1 = Resistor [tolerance=±5% resistance=220 package=THT]
  R2 = Resistor [tolerance=±5% resistance=220 package=THT]
  R3 = Resistor [tolerance=±5% resistance=220 package=THT]
  LED1 = LED - 3mm [color="Red (633nm)" package="3 mm [THT]"]
  LED2 = LED - 3mm [color="Green (555nm)" package="3 mm [THT]"]
  LED3 = LED - 3mm [color="Orange (620nm)" package="3 mm [THT]"]
  Componente1 = Arduino Uno (Rev3)
  Componente3 = ACS712 Low Current Sensor Board v12  # not connected
  GND = MicroSD Card Module

nets:
  GND: S1.Pin_1, S1.Pin_2, PCB2.GND, LED1.cathode, LED2.cathode, LED3.cathode, Componente1.GND, GND.GND
  N1: S1.Pin_3, S1.Pin_4, Componente1.RESET
  VCC: PCB2.VCC, Componente1.5V, GND.VCC
  N2: PCB2.RST, Componente1.D5_PWM
  N3: PCB2.DAT, Componente1.D6_PWM
  N4: PCB2.CLK, Componente1.D7
  N5: R1.Pin_0, Componente1.D10_PWM/SS
  N6: R1.Pin_1, LED1.anode
  N7: R2.Pin_0, Componente1.D8
  N8: R2.Pin_1, LED3.anode
  N9: R3.Pin_0, Componente1.D9_PWM
  N10: R3.Pin_1, LED2.anode
  N11: Componente1.D11_PWM/MOSI, GND.MOSI
  N12: Componente1.D12/MISO, GND.MISO
  N13: Componente1.D13/SCK, GND.SCK
  N14: Componente1.D4, GND.CS

custom parts:
  RTC_DS1302_module: Arduino module DS1302 SPI Real Time Clock

// code stored in the sketch: RELOJ_MICROSD2.ino
#include <SPI.h>
#include <SD.h>

File myFile;
#include <virtuabotixRTC.h> //Libreria para el reloj DS1302

virtuabotixRTC myRTC(7, 6, 5); // Pines del reloj CLK(7), DATA(6) RST(5)
int ledy = 8;   // Led Amarillo
int ledg = 9;   // Led Verde
int ledr = 10;  // Led Rojo

int sdpin = 4; // Puerto de comunicación Micro SD

void setup() {
  Serial.begin(9600);

  pinMode(ledy, OUTPUT);
  pinMode(ledg, OUTPUT);
  pinMode(ledr, OUTPUT);

  while (!Serial) {
    ; // wait for serial port to connect. Needed for native USB port only
  }

  Serial.print("Iniciando tarjeta Micro SD... ");

  if (!SD.begin(sdpin)) {
    Serial.println(" inicialización fallida!");
    digitalWrite(ledr, HIGH);
    while (1);
  }

  Serial.println("inicialización correcta!.");
  digitalWrite(ledr, HIGH);
  digitalWrite(ledg, HIGH);
  digitalWrite(ledy, HIGH);
  delay(100);
  digitalWrite(ledr, LOW);
  //  digitalWrite(ledg, LOW);
  // digitalWrite(ledy, LOW);
  delay(100);
  digitalWrite(ledr, HIGH);
  //  digitalWrite(ledg, HIGH);
  //  digitalWrite(ledy, HIGH);
  delay(100);
  //  digitalWrite(ledr, LOW);
  digitalWrite(ledg, LOW);
  //  digitalWrite(ledy, LOW);
  delay(100);
  //  digitalWrite(ledr, HIGH);
  digitalWrite(ledg, HIGH);
  //  digitalWrite(ledy, HIGH);
  delay(100);
  //digitalWrite(ledr, LOW);
  //  digitalWrite(ledg, LOW);
  digitalWrite(ledy, LOW);
  delay(100);
  digitalWrite(ledr, HIGH);
  digitalWrite(ledg, HIGH);
  digitalWrite(ledy, HIGH);
  delay(100);
  digitalWrite(ledr, LOW);
  digitalWrite(ledg, LOW);
  digitalWrite(ledy, LOW);
  delay(100);
  digitalWrite(ledr, HIGH);
  digitalWrite(ledg, HIGH);
  digitalWrite(ledy, HIGH);
  delay(100);
  digitalWrite(ledr, LOW);
  digitalWrite(ledg, LOW);
  digitalWrite(ledy, LOW);
  delay(100);
  digitalWrite(ledr, HIGH);
  digitalWrite(ledg, HIGH);
  digitalWrite(ledy, HIGH);
  delay(100);
  digitalWrite(ledr, LOW);
  digitalWrite(ledg, LOW);
  digitalWrite(ledy, LOW);
  delay(100);
  digitalWrite(ledr, HIGH);
  digitalWrite(ledg, HIGH);
  digitalWrite(ledy, HIGH);
  delay(100);
  digitalWrite(ledr, LOW);
  digitalWrite(ledg, LOW);
  // digitalWrite(ledy, LOW);
  delay(500);
  // Set the current date, and time in the following format:
  // seconds, minutes, hours, day of the week, day of the month, month, year
  // (14H, 27 Min, 30 Seg, DIA DOS (LUNES) 30/07/2018)
   myRTC.setDS1302Time(30, 27, 14, 2, 30, 7, 2018); // Descomentar esta linea para ajustar fecha y hora
}

void loop() {
  myRTC.updateTime(); // La funcion myRTC.updateTime() Jala la fecha y hora del DS3102.
  verifisd(); // Funcion que valida la SD instalada

  // De aqui para abajo Imprime y en Serial y guarda la mi MicroSD
  myFile = SD.open("9999.txt", FILE_WRITE); // Abre un archivo y si no existe lo crea con el nombre 9999.txt
  if (myFile) {
    // Comienza a escribir/guardar
    Serial.print("9999, ");
    Serial.print(myRTC.dayofmonth);
    Serial.print("/");
    Serial.print(myRTC.month);
    Serial.print("/");
    Serial.print(myRTC.year);
    Serial.print(", ");
    Serial.print(myRTC.hours);
    Serial.print(":");
    Serial.print(myRTC.minutes);
    Serial.print(":");
    Serial.print(myRTC.seconds);
    Serial.println(", ");

    myFile.print("9999, ");
    myFile.print(myRTC.dayofmonth);
    myFile.print("/");
    myFile.print(myRTC.month);
    myFile.print("/");
    myFile.print(myRTC.year);
    myFile.print(", ");
    myFile.print(myRTC.hours);
    myFile.print(":");
    myFile.print(myRTC.minutes);
    myFile.print(":");
    myFile.print(myRTC.seconds);
    myFile.println(", ");
    myFile.close();

    digitalWrite(ledg, HIGH);
    delay(500);
    digitalWrite(ledg, LOW);
    delay(500);
  }
  else {
    Serial.println("Error abriendo archivo de texto");
    digitalWrite(ledr, HIGH);
  }
}
void verifisd() {
  if (!SD.begin(4)) {
    Serial.println("Error en MicroSD");
    digitalWrite(ledr, HIGH);
    while (1);
  }
}
